# Fritzing sketch O Exoander (saved by Fritzing 0.9.1b)
breadboards: 1

parts:
  MCP2 = MCP2551 [package="DIP (Dual Inline) [THT]"]
  XTAL1 = Crystal [frequency="16 Mhz" package=THT]
  C3 = Ceramic Capacitor [capacitance=100nF package="100 mil [THT, multilayer]"]
  C4 = Ceramic Capacitor [capacitance=100nF package="100 mil [THT, multilayer]"]
  R1 = Resistor [tolerance=±5% resistance=4.7k package=THT]
  R2 = Resistor [tolerance=±5% resistance=100 package=THT]
  R3 = Resistor [tolerance=±5% resistance=100 package=THT]
  C5 = Ceramic Capacitor [capacitance=560pF package="100 mil [THT, multilayer]"]
  C6 = Ceramic Capacitor [capacitance=0.56nF package="100 mil [THT, multilayer]"]
  IC1 = IC, DIP package, 14 pins [chip_label=MCP250xx]

nets:
  N1: MCP2.TXD, IC1.pin13
  N2: MCP2.Vss, C3.0, R1.Pin_0, C5.0, C6.0, IC1.pin7
  N3: MCP2.Vdd, IC1.pin14
  N4: MCP2.RXD, IC1.pin12
  N5: MCP2.CANL, R2.Pin_0
  N6: MCP2.CANH, R3.Pin_0
  N7: MCP2.Rs, R1.Pin_1
  N8: XTAL1.pin_0, C3.1, IC1.pin9
  N9: XTAL1.pin_1, C4.1, IC1.pin8
  N10: R2.Pin_1, C6.1
  N11: R3.Pin_1, C5.1

custom parts:
  MCP2551: A DIP stand-in part for whatever IC you want. With 8 pins on a 300mil dual inline package (DIP) footprint.
