# Fritzing sketch O Expander (saved by Fritzing 0.9.1b)
circuit board: 6.84942cm x 7.37418cm
breadboards: 1

parts:
  MCP2 = MCP2551 [package="DIP (Dual Inline) [THT]"]
  XTAL1 = Crystal [frequency="16 Mhz" package=THT]
  C3 = Ceramic Capacitor [capacitance=100nF package="100 mil [THT, multilayer]"]
  C4 = Ceramic Capacitor [capacitance=100nF package="100 mil [THT, multilayer]"]
  R1 = Resistor [tolerance=±5% resistance=4.7k package=THT]
  R2 = Resistor [tolerance=±5% resistance=100 package=THT]
  R3 = Resistor [tolerance=±5% resistance=100 package=THT]
  C5 = Ceramic Capacitor [capacitance=560pF package="100 mil [THT, multilayer]"]
  C6 = Ceramic Capacitor [capacitance=0.56nF package="100 mil [THT, multilayer]"]
  IC1 = IC, DIP package, 14 pins [chip_label=MCP250xx]
  C7 = Electrolytic Capacitor [capacitance=10µF package="100 mil [THT, electrolytic]"]
  C9 = Electrolytic Capacitor [capacitance=0.1mF package="100 mil [THT, electrolytic]"]
  D1 = Rectifier Diode [part_number=1N4148 package="300 mil [THT]"]
  IC3 = Voltage Regulator [package=to-220-alt]
  IC2 = IC, DIP package, 16 pins [chip_label=74HC4050]
  J1 = shrouded pin header, 6 pins [form="♂ (shrouded male)"]  # not connected

nets:
  N1: MCP2.TXD, IC1.pin13
  N2: MCP2.Vss, C3.0, R1.Pin_0, C5.0, C6.0, IC1.pin7, C7.-, C9.-, IC3.IN, IC2.pin8
  N3: MCP2.Vdd, IC1.pin14, C9.+, IC3.OUT, IC2.pin1
  N4: MCP2.RXD, IC1.pin12
  N5: MCP2.CANL, R2.Pin_0
  N6: MCP2.CANH, R3.Pin_0
  N7: MCP2.Rs, R1.Pin_1
  N8: XTAL1.pin_0, C3.1, IC1.pin9
  N9: XTAL1.pin_1, C4.1, IC1.pin8
  N10: R2.Pin_1, C6.1
  N11: R3.Pin_1, C5.1
  N12: IC1.pin1, IC2.pin3
  N13: IC1.pin2, IC2.pin5
  N14: IC1.pin3, IC2.pin7
  N15: IC1.pin4, IC2.pin9
  N16: IC1.pin5, IC2.pin11
  N17: IC1.pin6, IC2.pin14
  N18: C7.+, D1.cathode

custom parts:
  MCP2551: A DIP stand-in part for whatever IC you want. With 8 pins on a 300mil dual inline package (DIP) footprint.
