# Fritzing sketch Copia di GenericCAN (saved by Fritzing 0.9.1b)
breadboards: 1

parts:
  Componente1 = Arduino Pro Mini v13
  MCP1 = MCP2515 [package="DIP (Dual Inline) [THT]"]
  MCP2 = MCP2551 [package="DIP (Dual Inline) [THT]"]
  C1 = Ceramic Capacitor [capacitance=100nF package="100 mil [THT, multilayer]"]
  XTAL1 = Crystal [frequency="16 Mhz" package=THT]
  C3 = Ceramic Capacitor [capacitance=100nF package="100 mil [THT, multilayer]"]
  C4 = Ceramic Capacitor [capacitance=100nF package="100 mil [THT, multilayer]"]
  R1 = Resistor [tolerance=±5% resistance=4.7k package=THT]
  R2 = Resistor [tolerance=±5% resistance=100 package=THT]
  R3 = Resistor [tolerance=±5% resistance=100 package=THT]
  C5 = Ceramic Capacitor [capacitance=560pF package="100 mil [THT, multilayer]"]
  C6 = Ceramic Capacitor [capacitance=0.56nF package="100 mil [THT, multilayer]"]

nets:
  VSS: Componente1.GND, MCP1.Vss, MCP2.Vss, C1.0, C3.0, C4.0, R1.Pin_0, C5.0, C6.0
  N1: Componente1.RESET, MCP1.RESET
  VDD: Componente1.VCC, MCP1.Vdd, MCP2.Vdd, C1.1
  N2: Componente1.D13/SCK, MCP1.SCK
  N3: Componente1.D12/MISO, MCP1.SO
  N4: Componente1.D11_PWM/MOSI, MCP1.SI
  N5: Componente1.D10_PWM/SS, MCP1.CS
  N6: Componente1.D2, MCP1.INT
  N7: MCP1.TXCAN, MCP2.TXD
  N8: MCP1.RXCAN, MCP2.RXD
  N9: MCP1.OSC2, XTAL1.pin_0, C3.1
  N10: MCP1.OSC1, XTAL1.pin_1, C4.1
  N11: MCP2.CANL, R2.Pin_0
  N12: MCP2.CANH, R3.Pin_0
  N13: MCP2.Rs, R1.Pin_1
  N14: R2.Pin_1, C6.1
  N15: R3.Pin_1, C5.1

custom parts:
  MCP2515: A DIP stand-in part for whatever IC you want. With 18 pins on a 300mil dual inline package (DIP) footprint.
  MCP2551: A DIP stand-in part for whatever IC you want. With 8 pins on a 300mil dual inline package (DIP) footprint.
