# Fritzing sketch BaseRailboxCompactNoBusRev1.0 (saved by Fritzing 0.9.1b)
breadboards: 1

parts:
  J1 = molex pin header, 10 pins [form=molex]
  BUS_Connector = Generic shrouded header - 6 pins [form="♂ (shrouded male)" package=THT]

nets:
  N1: J1.pin9, BUS_Connector.12v
  N2: J1.pin10, BUS_Connector.GND

notes:
  IoThingsWare
  PID: 5770-xx - Rev: 1.0

custom parts:
  Generic shrouded header - 6 pins: Generic shrouded header
