# Fritzing sketch BaseWithTranceiverRailboxCompactNoBusRev1.0 (saved by Fritzing 0.9.1b)
circuit board: 7.88cm x 6.5cm
breadboards: 1

parts:
  J1 = molex pin header, 10 pins [form=molex]
  BUS_Connector = Generic shrouded header - 6 pins [form="♂ (shrouded male)" package=THT]
  C14 = Electrolytic Capacitor [capacitance=10µF package="100 mil [THT, electrolytic]"]
  C15 = Electrolytic Capacitor [capacitance=100µF package="100 mil [THT, electrolytic]"]
  D2 = Rectifier Diode [part_number=1N4148 package="300 mil [THT]"]
  MCP5 = MCP2551 [package="DIP (Dual Inline) [THT]"]
  R7 = Resistor [tolerance=±5% resistance=4.7k package=THT]
  R8 = Resistor [tolerance=±5% resistance=100 package=THT]
  R9 = Resistor [tolerance=±5% resistance=100 package=THT]
  C16 = Ceramic Capacitor [capacitance=560pF package="100 mil [THT, multilayer]"]
  C17 = Ceramic Capacitor [capacitance=560pF package="100 mil [THT, multilayer]"]
  IC7 = IC, DIP package, 14 pins [chip_label=MCP250xx]
  XTAL3 = Crystal [frequency="16 Mhz" package=THT]
  C18 = Ceramic Capacitor [capacitance=100nF package="100 mil [THT, multilayer]"]
  C19 = Ceramic Capacitor [capacitance=100nF package="100 mil [THT, multilayer]"]
  J2 = female pin header, 3 pins [form="♀ (female)"]

nets:
  N1: J1.pin9, BUS_Connector.12v, D2.anode
  GND: J1.pin10, BUS_Connector.GND, C14.-, C15.-, MCP5.Vss, R7.Pin_0, C16.0, C17.0, IC7.pin7, C18.0, C19.0, J2.pin2
  N2: BUS_Connector.CANL, MCP5.CANL, R9.Pin_1
  N3: BUS_Connector.CANH, MCP5.CANH, R8.Pin_1
  N4: C14.+, D2.cathode, J2.pin1
  N5: C15.+, MCP5.Vdd, IC7.pin14, J2.pin3
  N6: MCP5.TXD, IC7.pin13
  N7: MCP5.RXD, IC7.pin12
  N8: MCP5.Rs, R7.Pin_1
  N9: R8.Pin_0, C17.1
  N10: R9.Pin_0, C16.1
  N11: IC7.pin8, XTAL3.pin_1, C19.1
  N12: IC7.pin9, XTAL3.pin_0, C18.1

notes:
  IoThingsWare
  PID: 5770-xx - Rev: 1.0

custom parts:
  Generic shrouded header - 6 pins: Generic shrouded header
  MCP2551: A DIP stand-in part for whatever IC you want. With 8 pins on a 300mil dual inline package (DIP) footprint.
