# Fritzing sketch BaseWithTranceiverSaveRailboxCompactNoBusRev1.0 (saved by Fritzing 0.9.1b)
breadboards: 2

parts:
  J1 = molex pin header, 10 pins [form=molex]
  BUS_Connector = Generic shrouded header - 6 pins [form="♂ (shrouded male)" package=THT]
  MCP3 = MCP2551 [package="DIP (Dual Inline) [THT]"]  # not connected
  IC4 = IC, DIP package, 14 pins [chip_label=MCP250xx]
  MCP4 = MCP2551 [package="DIP (Dual Inline) [THT]"]
  XTAL2 = Crystal [frequency="16 Mhz" package=THT]
  C10 = Ceramic Capacitor [capacitance=100nF package="100 mil [THT, multilayer]"]
  C11 = Ceramic Capacitor [capacitance=100nF package="100 mil [THT, multilayer]"]
  R4 = Resistor [tolerance=±5% resistance=4.7k package=THT]
  R5 = Resistor [tolerance=±5% resistance=100 package=THT]
  R6 = Resistor [tolerance=±5% resistance=100 package=THT]
  C12 = Ceramic Capacitor [capacitance=0.56nF package="100 mil [THT, multilayer]"]
  C13 = Ceramic Capacitor [capacitance=560pF package="100 mil [THT, multilayer]"]
  IC5 = IC, DIP package, 16 pins [chip_label=74HC4050]
  IC6 = Voltage Regulator [package=to-220-alt]
  C14 = Electrolytic Capacitor [capacitance=10µF package="100 mil [THT, electrolytic]"]
  C15 = Electrolytic Capacitor [capacitance=0.1mF package="100 mil [THT, electrolytic]"]
  D2 = Rectifier Diode [part_number=1N4148 package="300 mil [THT]"]
  MCP5 = MCP2551 [package="DIP (Dual Inline) [THT]"]
  R7 = Resistor [tolerance=±5% resistance=4.7k package=THT]
  R8 = Resistor [tolerance=±5% resistance=100 package=THT]
  R9 = Resistor [tolerance=±5% resistance=100 package=THT]
  C16 = Ceramic Capacitor [capacitance=0.56nF package="100 mil [THT, multilayer]"]
  C17 = Ceramic Capacitor [capacitance=560pF package="100 mil [THT, multilayer]"]

nets:
  N1: J1.pin9, BUS_Connector.12v, D2.anode
  VSS: J1.pin10, BUS_Connector.GND, IC4.pin7, MCP4.Vss, C11.0, R4.Pin_0, C12.0, C13.0, IC5.pin8, IC6.IN, C14.-, C15.-, MCP5.Vss, R7.Pin_0, C16.0, C17.0
  N2: BUS_Connector.CANL, MCP5.CANL, R9.Pin_1
  N3: BUS_Connector.CANH, MCP5.CANH, R8.Pin_1
  N4: IC4.pin1, IC5.pin3
  N5: IC4.pin2, IC5.pin5
  N6: IC4.pin3, IC5.pin7
  N7: IC4.pin4, IC5.pin9
  N8: IC4.pin5, IC5.pin11
  N9: IC4.pin6, IC5.pin14
  N10: IC4.pin8, XTAL2.pin_1, C10.1
  N11: IC4.pin9, XTAL2.pin_0, C11.1
  N12: IC4.pin12, MCP4.RXD
  N13: IC4.pin13, MCP4.TXD
  VDD: IC4.pin14, MCP4.Vdd, IC5.pin1, IC6.OUT, C15.+, MCP5.Vdd
  N14: MCP4.CANL, R5.Pin_0
  N15: MCP4.CANH, R6.Pin_0
  N16: MCP4.Rs, R4.Pin_1
  N17: R5.Pin_1, C12.1
  N18: R6.Pin_1, C13.1
  N19: IC6.GND, C14.+, D2.cathode
  N20: MCP5.Rs, R7.Pin_1
  N21: R8.Pin_0, C17.1
  N22: R9.Pin_0, C16.1

notes:
  IoThingsWare
  PID: 5770-xx - Rev: 1.0

custom parts:
  Generic shrouded header - 6 pins: Generic shrouded header
  MCP2551: A DIP stand-in part for whatever IC you want. With 8 pins on a 300mil dual inline package (DIP) footprint.
