# Fritzing sketch CommandBoardRelayRev1.0 (saved by Fritzing 0.8.7b)
circuit board: 8.4cm x 4.6cm
breadboards: 1

parts:
  IC2 = IC, DIP package, 6 pins [chip_label=IC]
  IC3 = IC, DIP package, 6 pins [chip_label=IC]
  IC4 = IC, DIP package, 6 pins [chip_label=IC]
  IC5 = IC, DIP package, 6 pins [chip_label=IC]
  IC6 = IC, DIP package, 6 pins [chip_label=IC]
  R1 = Resistor [tolerance=±5% resistance=2.7k package=THT]
  R2 = Resistor [tolerance=±5% resistance=2.7k package=THT]
  R3 = Resistor [tolerance=±5% resistance=2.7k package=THT]
  R4 = Resistor [tolerance=±5% resistance=2.7k package=THT]
  IC7 = IC, DIP package, 6 pins [chip_label=IC]
  R5 = Resistor [tolerance=±5% resistance=2.7k package=THT]
  R6 = Resistor [tolerance=±5% resistance=2.7k package=THT]
  Componente1 = Arduino Pro Mini v13
  J1 = female pin header, 4 pins [form="♀ (female)"]
  Switches = screw terminal, 12 pins

nets:
  N1: IC2.pin1, R1.Pin_1
  N2: IC2.pin2, IC3.pin2, IC4.pin2, IC5.pin2, IC6.pin2, IC7.pin2, Componente1.GND, J1.pin4
  N3: IC2.pin4, Switches.pin2
  N4: IC2.pin6, Switches.pin1
  N5: IC3.pin1, R2.Pin_1
  N6: IC3.pin4, Switches.pin4
  N7: IC3.pin6, Switches.pin3
  N8: IC4.pin1, R3.Pin_1
  N9: IC4.pin4, Switches.pin6
  N10: IC4.pin6, Switches.pin5
  N11: IC5.pin1, R4.Pin_1
  N12: IC5.pin4, Switches.pin8
  N13: IC5.pin6, Switches.pin7
  N14: IC6.pin1, R5.Pin_1
  N15: IC6.pin4, Switches.pin10
  N16: IC6.pin6, Switches.pin9
  N17: R1.Pin_0, Componente1.D7
  N18: R2.Pin_0, Componente1.D6_PWM
  N19: R3.Pin_0, Componente1.D5_PWM
  N20: R4.Pin_0, Componente1.D4
  N21: IC7.pin1, R6.Pin_1
  N22: IC7.pin4, Switches.pin12
  N23: IC7.pin6, Switches.pin11
  N24: R5.Pin_0, Componente1.D3_PWM
  N25: R6.Pin_0, Componente1.D2
  N26: Componente1.DTR, Componente1.D0/TX, Componente1.D1/RX
  N27: Componente1.A4, J1.pin3
  N28: Componente1.A5, J1.pin2
  N29: Componente1.RAW, J1.pin1

notes:
  PID: 5759 - Rev: 1.0
