# Fritzing sketch CommandBoardTypeARev0.0 (saved by Fritzing 0.8.7b)
circuit board: 8.56cm x 5.39cm
breadboards: 1

parts:
  J2 = female pin header, 2 pins [form="♀ (female)"]
  J1 = female pin header, 4 pins [form="♀ (female)"]
  U1 = AD5206 Digital Potentiometer [maximum_resistance=10kΩ package="DIP28 [THT]"]
  Componente1 = Arduino Pro Mini v13
  Selectors = screw terminal, 12 pins

nets:
  N1: J2.pin1, J1.pin2
  N2: J2.pin2, J1.pin3
  N3: J1.pin1, Componente1.RAW
  GND: J1.pin4, U1.Gnd, Componente1.GND
  N4: U1.W6, Selectors.pin11
  N5: U1.B6, Selectors.pin12
  N6: U1.CS, Componente1.D10_PWM/SS
  VDD: U1.Vdd, Componente1.VCC
  N7: U1.SDI, Componente1.D11_PWM/MOSI
  N8: U1.CLK, Componente1.D13/SCK
  N9: U1.B5, Selectors.pin10
  N10: U1.W5, Selectors.pin9
  N11: U1.B3, Selectors.pin6
  N12: U1.W3, Selectors.pin5
  N13: U1.B1, Selectors.pin2
  N14: U1.W1, Selectors.pin1
  N15: U1.W2, Selectors.pin3
  N16: U1.B2, Selectors.pin4
  N17: U1.W4, Selectors.pin7
  N18: U1.B4, Selectors.pin8
  N19: Componente1.DTR, Componente1.D0/TX, Componente1.D1/RX

notes:
  Akhela
  PID: 5760 - Rev: 1.0
  Command Module - Selectors
