# Fritzing sketch CommunicationModuleBoardRev1.0 (saved by Fritzing 0.8.7b)
circuit board: 5.55978cm x 2.65717cm
breadboards: 1

parts:
  U1 = Voltage Regulator - 5V [package="TO220 [THT]"]
  Power_plug1 = Power plug
  S2 = Pushbutton [package="[THT]"]
  C2 = Electrolytic Capacitor [capacitance=10µF rated_voltage=35V package="100 mil [THT, electrolytic]"]
  C1 = Electrolytic Capacitor [capacitance=10µF rated_voltage=35V package="100 mil [THT, electrolytic]"]
  C6 = Ceramic Capacitor [capacitance=22pF rated_voltage=35V package="200 mil [THT, multilayer]"]
  C5 = Ceramic Capacitor [capacitance=22pF rated_voltage=35V package="200 mil [THT, multilayer]"]
  XTAL1 = Crystal [frequency="16 Mhz" package=THT]
  R2 = Resistor [tolerance=±5% resistance=1k package=THT]
  part = Resistor [tolerance=±5% resistance=220 package=THT]  # not connected
  J5 = female pin header, 4 pins [form="♀ (female)"]
  U2 = atmega328 [package=dip]
  C7 = Ceramic Capacitor [capacitance=100nF package="100 mil [THT, multilayer]"]
  J6 = male pin header, 6 pins [form="♂ (male)"]

nets:
  N1: U1.input_voltage, Power_plug1.VCC, C1.+
  GND: U1.GND, Power_plug1.GND, S2.Pin_3, S2.Pin_4, C2.-, C1.-, C6.0, C5.1, J5.pin4, U2.GND, J6.pin5, J6.pin6
  N2: U1.output_voltage, C2.+, R2.Pin_0, J5.pin1, U2.VCC, U2.AVCC, U2.AREF, J6.pin4
  N3: S2.Pin_1, S2.Pin_2, R2.Pin_1, U2.RESET, C7.1
  N4: C6.1, XTAL1.pin_0, U2.XLAT1
  N5: C5.0, XTAL1.pin_1, U2.XLAT2
  N6: J5.pin2, U2.A5
  N7: J5.pin3, U2.A4
  N8: U2.D0_(RX), J6.pin3
  N9: U2.D1_(TX), J6.pin2
  N10: C7.0, J6.pin1

notes:
  This is a breadboard Arduino without an FTDI chip. You can program the chip with a USB-Serial breakout board, by using an external programmer or by programming the MCU in an Arduino board and then popping it into this circuit. The power source should be at least 7 VDC. Related example: http://itp.nyu.edu/physcomp/Tutorials/ArduinoBreadboard
