# Fritzing sketch ConnectorsRailboxCompactNoBusRev1.0 (saved by Fritzing 0.9.1b)
circuit board: 7.88cm x 6.5cm
breadboards: 1

parts:
  CPU = Arduino Pro Mini v13
  J3 = male pin header, 10 pins [form="♂ (male)"]
  J1 = molex pin header, 10 pins [form=molex]
  J6 = female pin header, 12 pins [form="♀ (female)"]
  J7 = female pin header, 12 pins [form="♀ (female)"]
  J8 = female pin header, 4 pins [form="♀ (female)"]
  R1 = Resistor [tolerance=±5% resistance=4.7k package=THT]
  R2 = Resistor [tolerance=±5% resistance=4.7k package=THT]
  J9 = double row female pin header, 10 pins [form="♀ (female)"]
  J10 = double row female pin header, 10 pins [form="♀ (female)"]
  J11 = double row female pin header, 10 pins [form="♀ (female)"]
  J12 = double row female pin header, 12 pins [form="♀ (female)"]
  J13 = shrouded pin header, 6 pins [form="♂ (shrouded male)"]
  ^_RAW_-_v_VCC = male pin header, 3 pins [form="♂ (male)"]
  J5 = female pin header, 2 pins [form="♀ (female)"]

nets:
  N1: CPU.A4, J8.pin2, R2.Pin_1, J13.pin2
  N2: CPU.A5, J8.pin1, R1.Pin_1, J13.pin3
  N3: CPU.RAW, J7.pin1, ^_RAW_-_v_VCC.pin1
  N4: CPU.GND, J6.pin4, J7.pin2, J13.pin1
  N5: CPU.RESET, J6.pin3, J7.pin3
  N6: CPU.VCC, J7.pin4, R1.Pin_0, R2.Pin_0, ^_RAW_-_v_VCC.pin3
  N7: CPU.A3, J7.pin5
  N8: CPU.A2, J7.pin6
  N9: CPU.A1, J7.pin7
  N10: CPU.A0, J7.pin8
  N11: CPU.D13/SCK, J7.pin9
  N12: CPU.D12/MISO, J7.pin10
  N13: CPU.D11_PWM/MOSI, J7.pin11
  N14: CPU.D10_PWM/SS, J7.pin12
  N15: CPU.D9_PWM, J6.pin12
  N16: CPU.D8, J6.pin11
  N17: CPU.D7, J6.pin10
  N18: CPU.D6_PWM, J6.pin9
  N19: CPU.D5_PWM, J6.pin8
  N20: CPU.D4, J6.pin7
  N21: CPU.D3_PWM, J6.pin6
  N22: CPU.D2, J6.pin5
  N23: CPU.D1/RX, J6.pin2
  N24: CPU.D0/TX, J6.pin1
  N25: J3.pin1, J1.pin1
  N26: J3.pin2, J1.pin2
  N27: J3.pin3, J1.pin3
  N28: J3.pin4, J1.pin4
  N29: J3.pin5, J1.pin5
  N30: J3.pin6, J1.pin6
  N31: J3.pin7, J1.pin7
  N32: J3.pin8, J1.pin8
  N33: J3.pin9, J1.pin9
  N34: J3.pin10, J1.pin10
  N35: J8.pin3, J5.pin1
  N36: J8.pin4, J5.pin2
  N37: J9.pin1, J9.pin2, J9.pin3, J9.pin4, J9.pin5
  N38: J9.pin6, J9.pin7, J9.pin8, J9.pin9, J9.pin10
  N39: J10.pin1, J10.pin2, J10.pin3, J10.pin4, J10.pin5
  N40: J10.pin6, J10.pin7, J10.pin8, J10.pin9, J10.pin10
  N41: J11.pin1, J11.pin2, J11.pin3, J11.pin4, J11.pin5
  N42: J11.pin6, J11.pin7, J11.pin8, J11.pin9, J11.pin10
  N43: J12.pin1, J12.pin2, J12.pin3, J12.pin4, J12.pin5, J12.pin6
  N44: J12.pin7, J12.pin8, J12.pin9, J12.pin10, J12.pin11, J12.pin12
  N45: J13.pin4, ^_RAW_-_v_VCC.pin2

notes:
  IoThingsWare
  PID: 5760 - Rev: 2.0
