# Fritzing sketch CurrentSensorBoardRev1.0 (saved by Fritzing 0.8.7b)
circuit board: 9.78371cm x 3.91348cm
breadboards: 1

parts:
  CPU = Arduino Pro Mini v13
  Sensor_4 = female pin header, 3 pins [form="♀ (female)"]
  Network = female pin header, 4 pins [form="♀ (female)"]
  A7/A6 = female pin header, 2 pins [form="♀ (female)"]
  I2C = female pin header, 2 pins [form="♀ (female)"]
  Sensor_2 = female pin header, 3 pins [form="♀ (female)"]
  Sensor_1 = female pin header, 3 pins [form="♀ (female)"]
  Sensor_3 = female pin header, 3 pins [form="♀ (female)"]
  Sensor_5 = female pin header, 3 pins [form="♀ (female)"]
  Sensor_6 = female pin header, 3 pins [form="♀ (female)"]

nets:
  N1: CPU.RAW, Network.pin4
  N2: CPU.GND, Sensor_4.pin1, Network.pin1, Sensor_2.pin1, Sensor_1.pin1, Sensor_3.pin1, Sensor_5.pin1, Sensor_6.pin1
  N3: CPU.VCC, Sensor_4.pin3, Sensor_2.pin3, Sensor_1.pin3, Sensor_3.pin3, Sensor_5.pin3, Sensor_6.pin3
  N4: CPU.A3, Sensor_4.pin2
  N5: CPU.A2, Sensor_3.pin2
  N6: CPU.A1, Sensor_2.pin2
  N7: CPU.A0, Sensor_1.pin2
  N8: Network.pin2, I2C.pin1
  N9: Network.pin3, I2C.pin2
  N10: A7/A6.pin1, Sensor_5.pin2
  N11: A7/A6.pin2, Sensor_6.pin2

notes:
  Akhela
  PID: 5758 - Rev: 1.0
