# Fritzing sketch CurrentSensorConnectorRev2.0 (saved by Fritzing 0.8.7b)
circuit board: 5.13644cm x 2.06021cm
breadboards: 1

parts:
  J5 = male pin header, 3 pins [form="♂ (male)"]
  J4 = male pin header, 3 pins [form="♂ (male)"]
  J3 = male pin header, 3 pins [form="♂ (male)"]
  J2 = male pin header, 3 pins [form="♂ (male)"]
  J1 = male pin header, 3 pins [form="♂ (male)"]
  J6 = male pin header, 7 pins [form="♂ (male)"]

nets:
  N1: J5.pin1, J4.pin1, J3.pin1, J2.pin1, J1.pin1, J6.pin1
  N2: J5.pin2, J4.pin2, J3.pin2, J2.pin2, J1.pin2, J6.pin2
  N3: J5.pin3, J6.pin7
  N4: J4.pin3, J6.pin6
  N5: J3.pin3, J6.pin5
  N6: J2.pin3, J6.pin4
  N7: J1.pin3, J6.pin3

notes:
  PID: 5761 - Rev: 2.0
  IoThingsWare
