# Fritzing sketch FeedbackBoardRev0.0 (saved by Fritzing 0.8.7b)
circuit board: 8.4cm x 4.6cm
breadboards: 1

parts:
  IC2 = IC, DIP package, 6 pins [chip_label=IC]
  IC3 = IC, DIP package, 6 pins [chip_label=IC]
  IC4 = IC, DIP package, 6 pins [chip_label=IC]
  IC5 = IC, DIP package, 6 pins [chip_label=IC]
  IC6 = IC, DIP package, 6 pins [chip_label=IC]
  R1 = Resistor [tolerance=±5% resistance=2.7k package=THT]
  R2 = Resistor [tolerance=±5% resistance=2.7k package=THT]
  R3 = Resistor [tolerance=±5% resistance=2.7k package=THT]
  R4 = Resistor [tolerance=±5% resistance=2.7k package=THT]
  IC7 = IC, DIP package, 6 pins [chip_label=IC]
  R5 = Resistor [tolerance=±5% resistance=2.7k package=THT]
  R6 = Resistor [tolerance=±5% resistance=2.7k package=THT]
  Componente1 = Arduino Pro Mini v13
  U1 = AD5206 Digital Potentiometer [maximum_resistance=10kΩ package="DIP28 [THT]"]
  J2 = female pin header, 2 pins [form="♀ (female)"]
  J1 = female pin header, 4 pins [form="♀ (female)"]
  Switches = screw terminal, 12 pins
  Selectors = screw terminal, 12 pins

nets:
  N1: IC2.pin1, R1.Pin_1
  GND: IC2.pin3, IC3.pin3, IC4.pin3, IC5.pin3, IC6.pin3, IC7.pin3, Componente1.GND, U1.Gnd, J1.pin4
  N2: IC2.pin4, Switches.pin2
  N3: IC2.pin6, Switches.pin1
  N4: IC3.pin1, R2.Pin_1
  N5: IC3.pin4, Switches.pin4
  N6: IC3.pin6, Switches.pin3
  N7: IC4.pin1, R3.Pin_1
  N8: IC4.pin4, Switches.pin6
  N9: IC4.pin6, Switches.pin5
  N10: IC5.pin1, R4.Pin_1
  N11: IC5.pin4, Switches.pin8
  N12: IC5.pin6, Switches.pin7
  N13: IC6.pin1, R5.Pin_1
  N14: IC6.pin4, Switches.pin10
  N15: IC6.pin6, Switches.pin9
  N16: R1.Pin_0, Componente1.D7
  N17: R2.Pin_0, Componente1.D6_PWM
  N18: R3.Pin_0, Componente1.D5_PWM
  N19: R4.Pin_0, Componente1.D4
  N20: IC7.pin1, R6.Pin_1
  N21: IC7.pin4, Switches.pin12
  N22: IC7.pin6, Switches.pin11
  N23: R5.Pin_0, Componente1.D3_PWM
  N24: R6.Pin_0, Componente1.D2
  N25: Componente1.DTR, Componente1.D0/TX, Componente1.D1/RX
  N26: Componente1.RAW, J1.pin1
  VCC: Componente1.VCC, U1.Vdd
  N27: Componente1.D13/SCK, U1.CLK
  N28: Componente1.D11_PWM/MOSI, U1.SDI
  N29: Componente1.D10_PWM/SS, U1.CS
  N30: U1.W6, Selectors.pin11
  N31: U1.B6, Selectors.pin12
  N32: U1.B5, Selectors.pin10
  N33: U1.W5, Selectors.pin9
  N34: U1.B3, Selectors.pin6
  N35: U1.W3, Selectors.pin5
  N36: U1.B1, Selectors.pin2
  N37: U1.W1, Selectors.pin1
  N38: U1.W2, Selectors.pin3
  N39: U1.B2, Selectors.pin4
  N40: U1.W4, Selectors.pin7
  N41: U1.B4, Selectors.pin8
  N42: J2.pin1, J1.pin2
  N43: J2.pin2, J1.pin3

notes:
  Akhela
  PID: 5759 - Rev: 1.0
