# Fritzing sketch RelayConnectorRev1.0 (saved by Fritzing 0.8.7b)
circuit board: 4.57583cm x 3.08492cm
breadboards: 1

parts:
  J1 = screw terminal, 10 pins
  J2 = screw terminal, 6 pins
  IC4 = IC, DIP package, 6 pins [chip_label=IC]
  IC5 = IC, DIP package, 6 pins [chip_label=IC]
  IC3 = IC, DIP package, 6 pins [chip_label=IC]
  IC2 = IC, DIP package, 6 pins [chip_label=IC]
  IC1 = IC, DIP package, 6 pins [chip_label=IC]
  R5 = Resistor [tolerance=±5% resistance=2.7k package=THT]
  R6 = Resistor [tolerance=±5% resistance=2.7k package=THT]
  R3 = Resistor [tolerance=±5% resistance=2.7k package=THT]
  R2 = Resistor [tolerance=±5% resistance=2.7k package=THT]
  R1 = Resistor [tolerance=±5% resistance=2.7k package=THT]

nets:
  N1: J1.pin1, IC1.pin6
  N2: J1.pin2, IC1.pin4
  N3: J1.pin3, IC2.pin6
  N4: J1.pin4, IC2.pin4
  N5: J1.pin5, IC3.pin6
  N6: J1.pin6, IC3.pin4
  N7: J1.pin7, IC4.pin6
  N8: J1.pin8, IC4.pin4
  N9: J1.pin9, IC5.pin6
  N10: J1.pin10, IC5.pin4
  N11: J2.pin1, R1.Pin_0
  N12: J2.pin2, R2.Pin_0
  N13: J2.pin3, R3.Pin_0
  N14: J2.pin4, R6.Pin_0
  N15: J2.pin5, R5.Pin_0
  N16: J2.pin6, IC4.pin2, IC5.pin2, IC3.pin2, IC2.pin2, IC1.pin2
  N17: IC4.pin1, R6.Pin_1
  N18: IC5.pin1, R5.Pin_1
  N19: IC3.pin1, R3.Pin_1
  N20: IC2.pin1, R2.Pin_1
  N21: IC1.pin1, R1.Pin_1

notes:
  Akhela
  PID: 5762 - Rev: 1.0
