# Fritzing sketch RelayConnectorRev2.0 (saved by Fritzing 0.8.7b)
circuit board: 4.58524cm x 3.13195cm
breadboards: 1

parts:
  IC4 = IC, DIP package, 6 pins [chip_label=IC]
  IC5 = IC, DIP package, 6 pins [chip_label=IC]
  IC3 = IC, DIP package, 6 pins [chip_label=IC]
  IC2 = IC, DIP package, 6 pins [chip_label=IC]
  IC1 = IC, DIP package, 6 pins [chip_label=IC]
  R5 = Resistor [tolerance=±5% resistance=2.7k package=THT]
  R6 = Resistor [tolerance=±5% resistance=2.7k package=THT]
  R3 = Resistor [tolerance=±5% resistance=2.7k package=THT]
  R2 = Resistor [tolerance=±5% resistance=2.7k package=THT]
  R1 = Resistor [tolerance=±5% resistance=2.7k package=THT]
  J2 = screw terminal, 6 pins
  J1 = screw terminal, 10 pins

nets:
  N1: IC4.pin1, R6.Pin_1
  N2: IC4.pin2, IC5.pin2, IC3.pin2, IC2.pin2, IC1.pin2, J2.pin6
  N3: IC4.pin4, J1.pin8
  N4: IC4.pin6, J1.pin7
  N5: IC5.pin1, R5.Pin_1
  N6: IC5.pin4, J1.pin10
  N7: IC5.pin6, J1.pin9
  N8: IC3.pin1, R3.Pin_1
  N9: IC3.pin4, J1.pin6
  N10: IC3.pin6, J1.pin5
  N11: IC2.pin1, R2.Pin_1
  N12: IC2.pin4, J1.pin4
  N13: IC2.pin6, J1.pin3
  N14: IC1.pin1, R1.Pin_1
  N15: IC1.pin4, J1.pin2
  N16: IC1.pin6, J1.pin1
  N17: R5.Pin_0, J2.pin5
  N18: R6.Pin_0, J2.pin4
  N19: R3.Pin_0, J2.pin3
  N20: R2.Pin_0, J2.pin2
  N21: R1.Pin_0, J2.pin1

notes:
  PID: 5762 - Rev: 2.0
  IoThingsWare
