# Fritzing sketch SchemaGrove (saved by Fritzing 0.8.7b)
circuit board: 4.6cm x 2.7cm
breadboards: 1

parts:
  IC1 = IC, DIP package, 8 pins [chip_label=IC]
  J1 = male pin header, 4 pins [form="♂ (male)"]
  R1 = Resistor [tolerance=±5% resistance=220 package=THT]
  R2 = Resistor [tolerance=±5% resistance=220 package=THT]
  J2 = female pin header, 3 pins [form="♀ (female)"]

nets:
  N1: IC1.pin3, J2.pin2
  N2: IC1.pin4, J1.pin1, J2.pin3
  N3: IC1.pin5, J1.pin3, R1.Pin_1
  N4: IC1.pin7, J1.pin4, R2.Pin_1
  N5: IC1.pin8, J1.pin2, R1.Pin_0, R2.Pin_0, J2.pin1

notes:
  Akhela
  PID: 5757
