# Fritzing sketch SelectorConnectorRev1.0 (saved by Fritzing 0.8.7b)
circuit board: 4.28329cm x 2.21447cm
breadboards: 1

parts:
  U1 = AD5206 Digital Potentiometer [maximum_resistance=10kΩ package="DIP28 [THT]"]
  J1 = female pin header, 5 pins [form="♀ (female)"]
  Selectors = screw terminal, 10 pins

nets:
  N1: U1.Gnd, J1.pin1
  N2: U1.CS, J1.pin3
  N3: U1.Vdd, J1.pin2
  N4: U1.SDI, J1.pin4
  N5: U1.CLK, J1.pin5
  N6: U1.B5, Selectors.pin10
  N7: U1.W5, Selectors.pin9
  N8: U1.B3, Selectors.pin6
  N9: U1.W3, Selectors.pin5
  N10: U1.B1, Selectors.pin2
  N11: U1.W1, Selectors.pin1
  N12: U1.W2, Selectors.pin3
  N13: U1.B2, Selectors.pin4
  N14: U1.W4, Selectors.pin7
  N15: U1.B4, Selectors.pin8

notes:
  Akhela
  PID: 5763 - Rev: 1.0
