# Fritzing sketch SelectorConnectorRev1.1 (saved by Fritzing 0.9.0b)
circuit board: 3.50247cm x 2.28033cm
breadboards: 1

parts:
  Digital_Potentiometer = AD5206 Digital Potentiometer [maximum_resistance=10kΩ package="DIP28 [THT]"]
  J1 = female pin header, 5 pins [form="♀ (female)"]
  Selectors = screw terminal, 10 pins

nets:
  N1: Digital_Potentiometer.Gnd, J1.pin1
  N2: Digital_Potentiometer.CS, J1.pin3
  N3: Digital_Potentiometer.Vdd, J1.pin2
  N4: Digital_Potentiometer.SDI, J1.pin4
  N5: Digital_Potentiometer.CLK, J1.pin5
  N6: Digital_Potentiometer.B5, Selectors.pin10
  N7: Digital_Potentiometer.W5, Selectors.pin9
  N8: Digital_Potentiometer.B3, Selectors.pin6
  N9: Digital_Potentiometer.W3, Selectors.pin5
  N10: Digital_Potentiometer.B1, Selectors.pin2
  N11: Digital_Potentiometer.W1, Selectors.pin1
  N12: Digital_Potentiometer.W2, Selectors.pin3
  N13: Digital_Potentiometer.B2, Selectors.pin4
  N14: Digital_Potentiometer.W4, Selectors.pin7
  N15: Digital_Potentiometer.B4, Selectors.pin8

notes:
  Akhela
  PID: 5763 - Rev: 1.1
