# Fritzing sketch SelectorConnectorRev2.prova (saved by Fritzing 0.8.7b)
circuit board: 3.96395cm x 2.05785cm
breadboards: 1

parts:
  Digital_Potentiometer = AD5206 Digital Potentiometer [maximum_resistance=10kΩ package="DIP28 [THT]"]
  J1 = female pin header, 5 pins [form="♀ (female)"]
  J2 = male pin header, 10 pins [form="♂ (male)"]

nets:
  N1: Digital_Potentiometer.A6, Digital_Potentiometer.A5, Digital_Potentiometer.A3, Digital_Potentiometer.A1, Digital_Potentiometer.A2, Digital_Potentiometer.A4, J2.pin1
  N2: Digital_Potentiometer.W6, J2.pin8
  N3: Digital_Potentiometer.B6, Digital_Potentiometer.B5, Digital_Potentiometer.B3, Digital_Potentiometer.B1, Digital_Potentiometer.B2, Digital_Potentiometer.B4, J2.pin2
  N4: Digital_Potentiometer.Gnd, J1.pin1
  N5: Digital_Potentiometer.CS, J1.pin3
  N6: Digital_Potentiometer.Vdd, J1.pin2
  N7: Digital_Potentiometer.SDI, J1.pin4
  N8: Digital_Potentiometer.CLK, J1.pin5
  N9: Digital_Potentiometer.W5, J2.pin7
  N10: Digital_Potentiometer.W3, J2.pin5
  N11: Digital_Potentiometer.W1, J2.pin3
  N12: Digital_Potentiometer.W2, J2.pin4
  N13: Digital_Potentiometer.W4, J2.pin6

notes:
  IoThingware
  PID: 5763 - Rev: 1.1
